# Fritzing sketch Schematics (saved by Fritzing 0.9.3b)

parts:
  Nano1 = Arduino Nano v2.3
  Componente1 = InvenSense MPU6050
  U1 = LIPO-110mAh [package=lipo-110]
  LED1 = RGB LED (com. cathode, rgb) [package="5 mm [THT]"]
  U2 = ESP8266 ESP-01 Upgraded WiFi Module [part_number=ESP8266]
  M1 = TP4056 Module [part_number=HW-107]
  S1 = Pushbutton [package="[THT]"]
  R1 = Resistor [tolerance=±20% resistance=1k package=THT]
  S3 = Toggle Switch [package=THT]
  U3 = Voltage Regulator -- 3.3 V -- LM1117

nets:
  GND: Nano1.GND, Componente1.GND, U2.GND, M1.OUT-#1, R1.Pin_1, U3.GND
  N1: Nano1.D2, S1.Pin_1, S1.Pin_2, R1.Pin_0
  N2: Nano1.D6, LED1.red_anode
  N3: Nano1.D7, LED1.green_anode
  N4: Nano1.D8, LED1.blue_anode
  N5: Nano1.D10, U2.TXD
  N6: Nano1.D11, U2.RXD
  N7: Nano1.A5, Componente1.SCL
  N8: Nano1.A4, Componente1.SDA
  +5V: Nano1.+5V, Componente1.VCC, S3.COM
  N9: U1.+, M1.BAT+
  N10: U1.-, M1.BAT-
  N11: U2.VCC, U3.OUT
  N12: M1.OUT-#4, S3.L1

custom parts:
  ESP8266 ESP-01 Upgraded WiFi Module: Upgraded Version ESP-01,all Flash are upgraded to 1M byte.Also support Cloud service remote transmission.
  TP4056 Module: TP4056 Lithium Battery Charge Management Module Links: TP4056 website
  Voltage Regulator -- 3.3 V -- LM1117: LM1117-3.3 Voltage regulator, 3.3 V output. Note that the pinout order is not the same as LM7805 or LM7833.
